# Fritzing sketch DigitalThermometer2 (saved by Fritzing 0.9.5d)
breadboards: 1

parts:
  Part1 = Arduino Uno (Rev3)
  DHT11_2 = DHT11 module
  LED1 = smd LED [color="Red (633nm)" package="1206 [SMD]"]

nets:
  N1: Part1.D2, DHT11_2.DATA
  N2: Part1.D6_PWM, LED1.cathode
  5V: Part1.5V, DHT11_2.VCC
  GND: Part1.GND, DHT11_2.GND, LED1.anode

custom parts:
  DHT11 module: DHT11 black pcb module
